// Logisim project 电路设计.circ as structural Verilog
// R
module \寄存器组  (
  input  [1:0] RA,
  input  [1:0] RB,
  input  [15:0] busw,
  input  WE,
  input  [1:0] RW,
  input  Clk,
  input  \清零 ,
  output [15:0] R0,
  output [15:0] busA,
  output [15:0] R1,
  output [15:0] busB,
  output [15:0] R2,
  output [15:0] R3
);

  wire and_1_out, and_2_out, and_3_out, and_4_out, decoder_1_out0, decoder_1_out1, decoder_1_out2,
       decoder_1_out3;

  Decoder #(.select(2)) decoder_1 (
    .out0(decoder_1_out0), .out1(decoder_1_out1), .out2(decoder_1_out2), .out3(decoder_1_out3), .sel(RW));  // open: en
  and and_1 (and_1_out, WE, decoder_1_out0);
  and and_2 (and_2_out, WE, decoder_1_out1);
  and and_3 (and_3_out, WE, decoder_1_out2);
  and and_4 (and_4_out, WE, decoder_1_out3);
  Register #(.width(16), .trigger("falling")) u_R0 (.D(busw), .en(and_1_out), .Q(R0), .clk(Clk), .clr(\清零 ));
  Register #(.width(16), .trigger("falling")) u_R1 (.D(busw), .en(and_2_out), .Q(R1), .clk(Clk), .clr(\清零 ));
  Register #(.width(16), .trigger("falling")) u_R2 (.D(busw), .en(and_3_out), .Q(R2), .clk(Clk), .clr(\清零 ));
  Register #(.width(16), .trigger("falling")) u_R3 (.D(busw), .en(and_4_out), .Q(R3), .clk(Clk), .clr(\清零 ));
  Multiplexer #(.select(2), .width(16)) multiplexer_1 (
    .in0(R0), .in1(R1), .in2(R2), .in3(R3), .out(busA), .sel(RA));  // open: en
  Multiplexer #(.select(2), .width(16)) multiplexer_2 (
    .in0(R0), .in1(R1), .in2(R2), .in3(R3), .out(busB), .sel(RB));  // open: en
endmodule

module \_16位ALU  (
  input  [3:0] S3_S0,
  input  [15:0] X,
  input  [15:0] Y,
  output SF,
  output OF,
  output CF,
  output [15:0] F,
  output ZF
);

  wire n74ls181_1_cn_4, n74ls181_2_cn_4, n74ls181_3_cn_4, n74ls181_4_cn_4, s3_s0_1_cn, s3_s0_1_m;
  wire [1:0] s3_s0_1_sel0;
  wire [2:0] n74ls181_1_f;
  wire [3:0] n74ls181_2_f, n74ls181_3_f, n74ls181_4_f, s3_s0_1_s00;
  wire [15:0] shifter_1_out, shifter_2_out, shifter_3_out;

  S3_S0 s3_s0_1 (
    .S3(S3_S0[3]), .S2(S3_S0[2]), .S1(S3_S0[1]), .S0(S3_S0[0]), .Cn(s3_s0_1_cn), .M(s3_s0_1_m),
    .S30(s3_s0_1_s00[3]), .S20(s3_s0_1_s00[2]), .S10(s3_s0_1_s00[1]), .S00(s3_s0_1_s00[0]),
    .SEL1(s3_s0_1_sel0[1]), .SEL0(s3_s0_1_sel0[0]));
  Shifter #(.width(16)) shifter_1 (.in(X), .\dist (Y[3:0]), .out(shifter_1_out));
  Shifter #(.width(16), .shift("lr")) shifter_2 (.in(X), .\dist (Y[3:0]), .out(shifter_2_out));
  Shifter #(.width(16), .shift("ar")) shifter_3 (.in(X), .\dist (Y[3:0]), .out(shifter_3_out));
  _74LS181 u_74ls181_1 (
    .A(X[15:12]), .B(Y[15:12]), .Cn(n74ls181_2_cn_4), .M(s3_s0_1_m), .Cn_4(n74ls181_1_cn_4),
    .S3_S0(s3_s0_1_s00), .F({SF, n74ls181_1_f}));  // open: A_B, P, G
  Multiplexer #(.select(2), .width(16)) multiplexer_1 (
    .in0({SF, n74ls181_1_f, n74ls181_2_f, n74ls181_3_f, n74ls181_4_f}), .in1(shifter_1_out),
    .in2(shifter_2_out), .in3(shifter_3_out), .out(F), .sel(s3_s0_1_sel0), .en(1'b1));
  _74LS181 u_74ls181_2 (
    .A(X[11:8]), .B(Y[11:8]), .Cn(n74ls181_3_cn_4), .M(s3_s0_1_m), .Cn_4(n74ls181_2_cn_4),
    .S3_S0(s3_s0_1_s00), .F(n74ls181_2_f));  // open: A_B, P, G
  _74LS181 u_74ls181_3 (
    .A(X[7:4]), .B(Y[7:4]), .Cn(n74ls181_4_cn_4), .M(s3_s0_1_m), .Cn_4(n74ls181_3_cn_4), .S3_S0(s3_s0_1_s00),
    .F(n74ls181_3_f));  // open: A_B, P, G
  _74LS181 u_74ls181_4 (
    .A(X[3:0]), .B(Y[3:0]), .Cn(s3_s0_1_cn), .M(s3_s0_1_m), .Cn_4(n74ls181_4_cn_4), .S3_S0(s3_s0_1_s00),
    .F(n74ls181_4_f));  // open: A_B, P, G
  \两位与形成零标志电路  u_ZF (
    .in_1(F[15]), .in_2(F[14]), .in_3(F[13]), .in_4(F[12]), .in_5(F[11]), .in_6(F[10]), .in_7(F[9]),
    .in_8(F[8]), .in_9(F[7]), .in_10(F[6]), .in_11(F[5]), .in_12(F[4]), .in_13(F[3]), .in_14(F[2]),
    .in_15(F[1]), .in_16(F[0]), .ZF(ZF));
  \OF溢出标志  \of溢出标志_1  (.SUB(S3_S0[0]), .Fa(X[12]), .Fb(Y[12]), .Ff(SF), .OF(OF));
  \进位  \u_进位_1  (.Sub(S3_S0[0]), .Cn(n74ls181_1_cn_4), .CF(CF));
endmodule

module _74LS181 (
  input  [3:0] A,
  input  [3:0] B,
  input  Cn,
  input  M,
  input  [3:0] S3_S0,
  output A_B,
  output P,
  output Cn_4,
  output G,
  output [3:0] F
);

  wire and_1_out, and_2_out, and_3_out, and_4_out, and_5_out, and_6_out, and_7_out, and_8_out, and_9_out,
       and_10_out, and_12_out, and_13_out, and_14_out, and_15_out, and_16_out, and_17_out, and_18_out,
       and_19_out, and_20_out, and_21_out, and_22_out, and_23_out, and_24_out, and_25_out, and_26_out,
       and_27_out, and_28_out, and_29_out, and_30_out, and_31_out, and_32_out, and_33_out, and_34_out,
       and_35_out, and_36_out, and_37_out, and_38_out, nand_1_out, nand_3_out, nor_1_out, nor_2_out,
       nor_3_out, nor_4_out, nor_5_out, nor_6_out, nor_7_out, nor_8_out, nor_9_out, nor_10_out, nor_11_out,
       nor_12_out, not_1_out, not_2_out, not_3_out, not_4_out, not_5_out, not_6_out, not_7_out, not_8_out,
       not_9_out;

  not not_1 (not_1_out, M);
  and and_1 (and_1_out, A[0], A[0]);
  nand nand_1 (nand_1_out, Cn, not_1_out);
  xor xor_1 (F[0], nand_1_out, and_5_out);
  and and_2 (and_2_out, B[0], S3_S0[0]);
  and and_3 (and_3_out, S3_S0[1], not_3_out);
  nor nor_1 (nor_1_out, and_1_out, and_2_out, and_3_out);
  and and_4 (and_4_out, not_1_out, nor_1_out);
  not not_2 (not_2_out, nor_1_out);
  and and_5 (and_5_out, not_2_out, nor_2_out);
  not not_3 (not_3_out, B[0]);
  and and_6 (and_6_out, not_3_out, S3_S0[2], A[0]);
  nor nor_2 (nor_2_out, and_6_out, and_9_out);
  and and_7 (and_7_out, not_1_out, nor_2_out, Cn);
  nor nor_3 (nor_3_out, and_4_out, and_7_out);
  xor xor_2 (F[1], nor_3_out, and_10_out);
  and and_8 (and_8_out, A[1], A[1]);
  and and_9 (and_9_out, A[0], B[0], S3_S0[3]);
  not not_4 (not_4_out, nor_4_out);
  and and_10 (and_10_out, not_4_out, nor_6_out);
  // Probe on nor_5_out
  and and_11 (A_B, F[0], F[1], F[2], F[3]);
  and and_12 (and_12_out, S3_S0[1], not_5_out);
  and and_13 (and_13_out, B[1], S3_S0[0]);
  nor nor_4 (nor_4_out, and_8_out, and_13_out, and_12_out);
  and and_14 (and_14_out, not_1_out, nor_1_out, nor_6_out);
  and and_15 (and_15_out, not_1_out, nor_4_out);
  nor nor_5 (nor_5_out, and_15_out, and_14_out, and_17_out);
  xor xor_3 (F[2], nor_5_out, and_18_out);
  not not_5 (not_5_out, B[1]);
  and and_16 (and_16_out, not_5_out, S3_S0[2], A[1]);
  nor nor_6 (nor_6_out, and_16_out, and_20_out);
  and and_17 (and_17_out, not_1_out, Cn, nor_2_out, nor_6_out);
  not not_6 (not_6_out, nor_7_out);
  and and_18 (and_18_out, not_6_out, nor_9_out);
  // Probe on F[2]
  // Probe on B[3]
  and and_19 (and_19_out, A[2], A[2]);
  and and_20 (and_20_out, A[1], B[1], S3_S0[3]);
  and and_21 (and_21_out, not_1_out, nor_4_out, nor_9_out);
  and and_22 (and_22_out, not_1_out, nor_7_out);
  and and_23 (and_23_out, S3_S0[1], not_7_out);
  and and_24 (and_24_out, B[2], S3_S0[0]);
  nor nor_7 (nor_7_out, and_19_out, and_24_out, and_23_out);
  and and_25 (and_25_out, not_1_out, nor_1_out, nor_6_out, nor_9_out);
  nor nor_8 (nor_8_out, and_22_out, and_21_out, and_25_out, and_27_out);
  xor xor_4 (F[3], nor_8_out, and_28_out);
  not not_7 (not_7_out, B[2]);
  and and_26 (and_26_out, not_7_out, S3_S0[2], A[2]);
  nor nor_9 (nor_9_out, and_26_out, and_29_out);
  not not_8 (not_8_out, nor_10_out);
  and and_27 (and_27_out, not_1_out, Cn, nor_2_out, nor_6_out, nor_9_out);
  and and_28 (and_28_out, not_8_out, nor_11_out);
  and and_29 (and_29_out, A[2], B[2], S3_S0[3]);
  and and_30 (and_30_out, A[3], A[3]);
  nand nand_2 (P, nor_2_out, nor_6_out, nor_9_out, nor_11_out);
  and and_31 (and_31_out, B[3], S3_S0[0]);
  and and_32 (and_32_out, S3_S0[1], not_9_out);
  nor nor_10 (nor_10_out, and_30_out, and_31_out, and_32_out);
  nand nand_3 (nand_3_out, Cn, nor_2_out, nor_6_out, nor_9_out, nor_11_out);
  or or_1 (Cn_4, ~nand_3_out, ~nor_12_out);  // OR_Gate
  not not_9 (not_9_out, B[3]);
  and and_33 (and_33_out, not_9_out, S3_S0[2], A[3]);
  nor nor_11 (nor_11_out, and_33_out, and_36_out);
  and and_34 (and_34_out, nor_1_out, nor_6_out, nor_9_out, nor_11_out);
  and and_35 (and_35_out, nor_4_out, nor_9_out, nor_11_out);
  nor nor_12 (nor_12_out, and_34_out, and_35_out, and_38_out, and_37_out);
  not not_10 (G, nor_12_out);
  and and_36 (and_36_out, A[3], B[3], S3_S0[3]);
  and and_37 (and_37_out, nor_10_out, nor_10_out);
  and and_38 (and_38_out, nor_7_out, nor_11_out);
  // Probe on B[3]
endmodule

module \OF溢出标志  (
  input  SUB,
  input  Fa,
  input  Fb,
  input  Ff,
  output OF
);

  wire and_1_out, and_2_out, and_3_out, and_4_out, not_1_out, not_2_out, not_3_out, not_4_out, not_5_out,
       not_6_out, not_7_out, not_8_out;

  not not_1 (not_1_out, SUB);
  not not_2 (not_2_out, Fa);
  not not_3 (not_3_out, Fb);
  not not_4 (not_4_out, SUB);
  not not_5 (not_5_out, Ff);
  not not_6 (not_6_out, Fa);
  not not_7 (not_7_out, Fb);
  not not_8 (not_8_out, Ff);
  and and_1 (and_1_out, not_1_out, not_2_out, not_3_out, Ff);
  and and_2 (and_2_out, not_4_out, Fa, Fb, not_5_out);
  and and_3 (and_3_out, SUB, not_6_out, Fb, Ff);
  and and_4 (and_4_out, SUB, Fa, not_7_out, not_8_out);
  or or_1 (OF, and_1_out, and_2_out, and_3_out, and_4_out);
endmodule

module \ZF标志形成电路  (
  input  f15,
  input  f14,
  input  f13,
  input  f12,
  input  f11,
  input  f10,
  input  f9,
  input  f8,
  output Z
);

  wire not_1_out, not_2_out, not_3_out, not_4_out, not_5_out, not_6_out, not_7_out, not_8_out;

  not not_1 (not_1_out, f15);
  not not_2 (not_2_out, f14);
  not not_3 (not_3_out, f13);
  not not_4 (not_4_out, f12);
  not not_5 (not_5_out, f11);
  not not_6 (not_6_out, f10);
  not not_7 (not_7_out, f9);
  not not_8 (not_8_out, f8);
  and and_1 (Z, not_1_out, not_2_out, not_3_out, not_4_out, not_5_out, not_6_out, not_7_out, not_8_out);
endmodule

module S3_S0 (
  input  S3,
  input  S2,
  input  S1,
  input  S0,
  output Cn,
  output M,
  output S30,
  output S20,
  output S10,
  output S00,
  output SEL1,
  output SEL0
);

  wire and_1_out, and_2_out, and_5_out, and_6_out, and_7_out, and_8_out, and_9_out, not_1_out, not_2_out,
       not_3_out, not_4_out, not_5_out, not_6_out, not_7_out, not_8_out, not_9_out, not_10_out;

  not not_1 (not_1_out, S1);
  and and_1 (and_1_out, not_1_out, not_2_out);
  not not_2 (not_2_out, S0);
  and and_2 (and_2_out, S1, S0);
  not not_3 (not_3_out, S2);
  and and_3 (S30, not_3_out, not_4_out);
  not not_4 (not_4_out, S0);
  not not_5 (not_5_out, S1);
  and and_4 (S20, not_5_out, S0);
  not not_6 (not_6_out, S1);
  and and_5 (and_5_out, not_6_out, S0);
  and and_6 (and_6_out, S1, not_7_out);
  not not_7 (not_7_out, S0);
  not not_8 (not_8_out, S2);
  and and_7 (and_7_out, not_8_out, not_9_out);
  not not_9 (not_9_out, S0);
  and and_8 (and_8_out, S2, S1, S0);
  and and_9 (and_9_out, S2, S1, not_10_out);
  not not_10 (not_10_out, S0);
  or or_1 (Cn, and_1_out, and_2_out);
  or or_2 (S10, and_5_out, and_6_out);
  or or_3 (S00, and_7_out, S1);
  or or_4 (SEL1, and_8_out, S3);
  or or_5 (SEL0, and_9_out, S3);

  assign M = S2;
endmodule

module \两位与形成零标志电路  (
  input  in_1,
  input  in_2,
  input  in_3,
  input  in_4,
  input  in_5,
  input  in_6,
  input  in_7,
  input  in_8,
  input  in_9,
  input  in_10,
  input  in_11,
  input  in_12,
  input  in_13,
  input  in_14,
  input  in_15,
  input  in_16,
  output ZF
);

  wire \zf标志形成电路_1_z , \zf标志形成电路_2_z ;

  \ZF标志形成电路  \zf标志形成电路_1  (
    .f15(in_1), .f14(in_2), .f13(in_3), .f12(in_4), .f11(in_5), .f10(in_6), .f9(in_7), .f8(in_8),
    .Z(\zf标志形成电路_1_z ));
  \ZF标志形成电路  \zf标志形成电路_2  (
    .f15(in_9), .f14(in_10), .f13(in_11), .f12(in_12), .f11(in_13), .f10(in_14), .f9(in_15), .f8(in_16),
    .Z(\zf标志形成电路_2_z ));
  and and_1 (ZF, \zf标志形成电路_1_z , \zf标志形成电路_2_z );
endmodule

module \进位  (
  input  Sub,
  input  Cn,
  output CF
);

  wire and_1_out, and_2_out, not_1_out, not_2_out;

  not not_1 (not_1_out, Sub);
  not not_2 (not_2_out, Cn);
  and and_1 (and_1_out, not_1_out, not_2_out);
  and and_2 (and_2_out, Sub, Cn);
  or or_1 (CF, and_1_out, and_2_out);
endmodule

module \R_type译码器  (
  input  func2,
  input  func1,
  input  func0,
  output S3,
  output S2,
  output S1,
  output S0,
  output Smux
);

  wire and_4_out, and_5_out, and_6_out, not_1_out, not_2_out, not_4_out, not_5_out, not_6_out;

  not not_1 (not_1_out, func0);
  not not_2 (not_2_out, func1);
  not not_3 (S1, func1);
  not not_4 (not_4_out, func2);
  not not_5 (not_5_out, func1);
  not not_6 (not_6_out, func0);
  and and_1 (Smux, func2, func1, func0);
  and and_2 (S3, func2, func1, not_1_out);
  and and_3 (S2, func2, not_2_out);
  and and_4 (and_4_out, not_4_out, not_5_out, not_6_out);
  and and_5 (and_5_out, func1, func0);
  and and_6 (and_6_out, func2, func0);
  or or_1 (S0, and_4_out, and_5_out, and_6_out);
endmodule

module \位扩展器  (
  input  [7:0] Imm,
  input  Exop,
  output [15:0] out_3
);

  wire [15:0] bit_extender_1_out, bit_extender_2_out;

  assign bit_extender_1_out = {{8{1'b0}}, Imm};  // Bit_Extender bit_extender_1
  assign bit_extender_2_out = {{8{Imm[7]}}, Imm};  // Bit_Extender bit_extender_2
  Multiplexer #(.width(16)) multiplexer_1 (
    .in0(bit_extender_1_out), .in1(bit_extender_2_out), .out(out_3), .sel(Exop));  // open: en
endmodule

module \数据通路  (
  input  in_1,
  input  in_2
);

  wire beq, bgt, bne, clock_1_out, d_ff_1_q, d_ff_1_qn, Exop, flag, Imux1, Imux2, jump, ld, Lmux, muxb,
       \n16位alu_1_sf , \n16位alu_1_zf , not_1_out, not_2_out, PC_1, R_type, Smux, str, WE, wpc, \译码器_1_pc_1 ;
  wire [1:0] RW;
  wire [3:0] S3_S0, \寄存器组_1_r0 , \寄存器组_1_r0_2 , \寄存器组_1_r1_2 , \寄存器组_1_r1_3 , \寄存器组_1_r2 , \寄存器组_1_r2_3 ,
       \寄存器组_1_r2_4 , \寄存器组_1_r3_2 , \寄存器组_1_r3_3 ;
  wire [7:0] \寄存器组_1_r1 ;
  wire [7:4] \寄存器组_1_r2_2 ;
  wire [11:0] adress;
  wire [15:0] multiplexer_1_out, multiplexer_2_out, multiplexer_3_out, multiplexer_4_out, multiplexer_5_out,
       multiplexer_6_out, \n16位alu_1_f , pc_1_pc, ram_1_data, \下地址逻辑_1_下地址 , \寄存器组_1_busa , \寄存器组_1_busb ,
       \寄存器组_1_r3 , \扩展器_out_3 ;
  wire [15:8] \寄存器组_1_r0_3 ;
  wire [15:12] rom_1_data;

  Hex_Digit_Display hex_digit_display_1 (.value(\寄存器组_1_r0_3 [15:12]));  // open: dp
  Hex_Digit_Display hex_digit_display_2 (.value(\寄存器组_1_r0_3 [11:8]));  // open: dp
  Hex_Digit_Display hex_digit_display_3 (.value(\寄存器组_1_r0_2 ));  // open: dp
  Clock clock_1 (.out(clock_1_out));
  Hex_Digit_Display hex_digit_display_4 (.value(\寄存器组_1_r1_3 ));  // open: dp
  Hex_Digit_Display hex_digit_display_5 (.value(\寄存器组_1_r0 ));  // open: dp
  Hex_Digit_Display hex_digit_display_6 (.value(\寄存器组_1_r1 [7:4]));  // open: dp
  Hex_Digit_Display hex_digit_display_7 (.value(\寄存器组_1_r1_2 ));  // open: dp
  Hex_Digit_Display hex_digit_display_8 (.value(\寄存器组_1_r1 [3:0]));  // open: dp
  Hex_Digit_Display hex_digit_display_9 (.value(\寄存器组_1_r2_3 ));  // open: dp
  Hex_Digit_Display hex_digit_display_10 (.value(\寄存器组_1_r2_4 ));  // open: dp
  Hex_Digit_Display hex_digit_display_11 (.value(\寄存器组_1_r2_2 ));  // open: dp
  Hex_Digit_Display hex_digit_display_12 (.value(\寄存器组_1_r2 ));  // open: dp
  \寄存器组  \u_寄存器组_1  (
    .busw(multiplexer_1_out), .WE(WE), .RW(RW), .Clk(d_ff_1_q), .RA(adress[11:10]), .RB(adress[9:8]),
    .\清零 (in_2), .R0({\寄存器组_1_r0_3 , \寄存器组_1_r0_2 , \寄存器组_1_r0 }), .busA(\寄存器组_1_busa ),
    .R1({\寄存器组_1_r1_3 , \寄存器组_1_r1_2 , \寄存器组_1_r1 }), .busB(\寄存器组_1_busb ),
    .R2({\寄存器组_1_r2_4 , \寄存器组_1_r2_3 , \寄存器组_1_r2_2 , \寄存器组_1_r2 }),
    .R3({\寄存器组_1_r3 [15:12], \寄存器组_1_r3_3 , \寄存器组_1_r3_2 , \寄存器组_1_r3 [3:0]}));
  Multiplexer #(.width(16)) multiplexer_1 (
    .in0(multiplexer_2_out), .in1(ram_1_data), .out(multiplexer_1_out), .sel(Lmux));  // open: en
  D_Flip_Flop d_ff_1 (
    .clk(clock_1_out), .D(d_ff_1_qn), .Q(d_ff_1_q), .Qn(d_ff_1_qn), .en(not_1_out));  // open: preset, reset
  not not_1 (not_1_out, flag);
  Hex_Digit_Display hex_digit_display_13 (.value(\寄存器组_1_r3 [15:12]));  // open: dp
  Hex_Digit_Display hex_digit_display_14 (.value(\寄存器组_1_r3_3 ));  // open: dp
  \位扩展器  \u_扩展器  (.Imm(adress[7:0]), .Exop(Exop), .out_3(\扩展器_out_3 ));
  Multiplexer #(.width(16)) multiplexer_2 (
    .in0(\n16位alu_1_f ), .in1(multiplexer_6_out), .out(multiplexer_2_out), .sel(Smux));  // open: en
  Hex_Digit_Display hex_digit_display_15 (.value(\寄存器组_1_r3 [3:0]));  // open: dp
  Hex_Digit_Display hex_digit_display_16 (.value(\寄存器组_1_r3_2 ));  // open: dp
  Multiplexer #(.width(16)) multiplexer_3 (
    .in0(\寄存器组_1_busa ), .in1(\扩展器_out_3 ), .out(multiplexer_3_out), .sel(Imux1));  // open: en
  Multiplexer #(.width(16)) multiplexer_4 (
    .in0(\寄存器组_1_busb ), .in1(\扩展器_out_3 ), .out(multiplexer_4_out), .sel(muxb));  // open: en
  Multiplexer #(.width(16)) multiplexer_5 (
    .in0(multiplexer_4_out), .in1(16'h8), .out(multiplexer_5_out), .sel(Imux2));  // open: en
  Multiplexer #(.width(16)) multiplexer_6 (
    .in0({16{1'b0}}), .in1(16'h1), .out(multiplexer_6_out), .sel(\n16位alu_1_sf ));  // open: en
  \_16位ALU  \u_16位alu_1  (
    .S3_S0(S3_S0), .X(multiplexer_3_out), .Y(multiplexer_5_out), .SF(\n16位alu_1_sf ), .F(\n16位alu_1_f ),
    .ZF(\n16位alu_1_zf ));  // open: OF, CF
  PC u_pc_1 (.wpc(wpc), .ADDR(\下地址逻辑_1_下地址 ), .pc_1(PC_1), .\清零 (in_1), .clk(d_ff_1_q), .PC(pc_1_pc));
  not not_2 (not_2_out, d_ff_1_q);
  \下地址逻辑  \u_下地址逻辑_1  (
    .pc(pc_1_pc), .offset(adress[7:0]), .address(adress), .beq(beq), .ZF(\n16位alu_1_zf ), .bne(bne),
    .jump(jump), .bgt(bgt), .SF(\n16位alu_1_sf ), .\下地址 (\下地址逻辑_1_下地址 ));
  RAM #(.addrWidth(16), .dataWidth(16), .bus("separate")) ram_1 (
    .addr(\n16位alu_1_f ), .din(\寄存器组_1_busb ), .data(ram_1_data), .str(str), .clk(not_2_out), .ld(ld));  // open: sel, clr
  ROM #(.addrWidth(16), .dataWidth(16)) rom_1 (.addr(pc_1_pc), .data({rom_1_data, adress}), .sel(1'b1));
  Multiplexer #(.width(2)) multiplexer_7 (.in0(adress[9:8]), .in1(adress[7:6]), .out(RW), .sel(R_type));  // open: en
  \译码器  \u_译码器_1  (
    .func(adress[2:0]), .OP(rom_1_data), .Smux(Smux), .S3_S0(S3_S0), .R_type(R_type), .Imux2(Imux2),
    .Imux1(Imux1), .PC_1(\译码器_1_pc_1 ), .muxb(muxb), .Exop(Exop), .str(str), .ld(ld), .Lmux(Lmux), .beq(beq),
    .bne(bne), .WE(WE), .wpc(wpc), .jump(jump), .bgt(bgt), .flag(flag));
  Multiplexer multiplexer_8 (.in0(\译码器_1_pc_1 ), .in1(1'b1), .out(PC_1), .sel(R_type));  // open: en

  // Other names for the same wires on the sheet: imm[7:0] = adress[7:0]; offset[7:0] = adress[7:0];
  //   rs[1:0] = adress[11:10]; rt[1:0] = adress[9:8]

  // Notes on the sheet:
  //   contents of rom_1 (hex, n*v repeats v):
  //   6400 6901 180 101 602 103 107 20ff 31f9 45f9 5501 7401 104 985 686 8503 0 0 0 9102 0 0 a402 0 0 b021
  //   7*0 c000
endmodule

module \下地址逻辑  (
  input  [15:0] pc,
  input  jump,
  input  [7:0] offset,
  input  [11:0] address,
  input  beq,
  input  bne,
  input  bgt,
  input  SF,
  input  ZF,
  output [15:0] \下地址 
);

  wire and_2_out, and_3_out, and_4_out, not_1_out, not_2_out, or_2_out;
  wire [15:0] adder_1_out, adder_2_out, and_1_out, bit_extender_1_out, bit_extender_2_out, multiplexer_1_out,
       or_1_out;

  assign bit_extender_1_out = {{8{offset[7]}}, offset};  // Bit_Extender bit_extender_1
  assign bit_extender_2_out = {{4{1'b0}}, address};  // Bit_Extender bit_extender_2
  Adder #(.width(16)) adder_1 (.a(pc), .b(16'h1), .out(adder_1_out));  // open: cin, cout
  Multiplexer #(.width(16)) multiplexer_1 (
    .in0(adder_1_out), .in1(adder_2_out), .out(multiplexer_1_out), .sel(or_2_out));  // open: en
  Adder #(.width(16)) adder_2 (.a(adder_1_out), .b(bit_extender_1_out), .out(adder_2_out));  // open: cin, cout
  assign and_1_out = adder_1_out & 16'hf000;  // AND_Gate and_1, 16 bits wide
  assign or_1_out = and_1_out | bit_extender_2_out;  // OR_Gate or_1, 16 bits wide
  and and_2 (and_2_out, beq, ZF);
  Multiplexer #(.width(16)) multiplexer_2 (
    .in0(multiplexer_1_out), .in1(or_1_out), .out(\下地址 ), .sel(jump));  // open: en
  or or_2 (or_2_out, and_2_out, and_4_out, and_3_out);
  and and_3 (and_3_out, bgt, not_2_out);
  and and_4 (and_4_out, bne, not_1_out);
  not not_1 (not_1_out, ZF);
  not not_2 (not_2_out, SF);
endmodule

module PC (
  input  wpc,
  input  [15:0] ADDR,
  input  pc_1,
  input  \清零 ,
  input  clk,
  output [15:0] PC
);

  wire not_1_out;

  Counter #(.width(16), .max('hffff)) counter_1 (
    .load(wpc), .D(ADDR), .count(pc_1), .Q(PC), .clk(not_1_out), .clr(\清零 ));  // open: carry
  not not_1 (not_1_out, clk);
endmodule

module \译码器  (
  input  [2:0] func,
  input  [3:0] OP,
  output Smux,
  output [3:0] S3_S0,
  output R_type,
  output Imux2,
  output Imux1,
  output PC_1,
  output muxb,
  output Exop,
  output str,
  output ld,
  output Lmux,
  output beq,
  output bne,
  output WE,
  output wpc,
  output jump,
  output bgt,
  output flag
);

  wire \r_type译码器_1_smux , \主译码器_1_smux ;
  wire [3:0] \r_type译码器_1_s0 , \主译码器_1_s0 ;

  Multiplexer multiplexer_1 (.in0(\主译码器_1_smux ), .in1(\r_type译码器_1_smux ), .out(Smux), .sel(R_type));  // open: en
  \主译码器  \u_主译码器_1  (
    .OP3(OP[3]), .OP2(OP[2]), .OP1(OP[1]), .OP0(OP[0]), .Smux(\主译码器_1_smux ), .S3(\主译码器_1_s0 [3]),
    .R_type(R_type), .Imux2(Imux2), .Imux1(Imux1), .S2(\主译码器_1_s0 [2]), .S1(\主译码器_1_s0 [1]), .PC_1(PC_1),
    .S0(\主译码器_1_s0 [0]), .muxb(muxb), .Exop(Exop), .str(str), .ld(ld), .Lmux(Lmux), .beq(beq), .bne(bne),
    .WE(WE), .wpc(wpc), .jump(jump), .bgt(bgt), .flag(flag));
  \R_type译码器  \r_type译码器_1  (
    .func2(func[2]), .func1(func[1]), .func0(func[0]), .S3(\r_type译码器_1_s0 [3]), .S2(\r_type译码器_1_s0 [2]),
    .S1(\r_type译码器_1_s0 [1]), .S0(\r_type译码器_1_s0 [0]), .Smux(\r_type译码器_1_smux ));
  Multiplexer #(.width(4)) multiplexer_2 (
    .in0(\主译码器_1_s0 ), .in1(\r_type译码器_1_s0 ), .out(S3_S0), .sel(R_type));  // open: en
endmodule

module \主译码器  (
  input  OP3,
  input  OP2,
  input  OP1,
  input  OP0,
  output Smux,
  output S3,
  output R_type,
  output Imux2,
  output Imux1,
  output S2,
  output S1,
  output PC_1,
  output S0,
  output muxb,
  output Exop,
  output str,
  output ld,
  output Lmux,
  output beq,
  output bne,
  output WE,
  output wpc,
  output jump,
  output bgt,
  output flag
);

  wire _0011_out, _0100_out, _0101_out, not_1_out, not_2_out, not_3_out, not_4_out, not_5_out, not_6_out,
       not_7_out, not_8_out, not_9_out, not_10_out, not_11_out, not_12_out, not_13_out, not_14_out,
       not_15_out, not_16_out, not_17_out, not_18_out, not_19_out, not_20_out, not_21_out, not_22_out,
       not_23_out, not_24_out, not_25_out, not_26_out, not_27_out;

  not not_1 (not_1_out, OP3);
  not not_2 (not_2_out, OP2);
  not not_3 (not_3_out, OP1);
  not not_4 (not_4_out, OP0);
  not not_5 (not_5_out, OP3);
  not not_6 (not_6_out, OP2);
  not not_7 (not_7_out, OP0);
  not not_8 (not_8_out, OP3);
  not not_9 (not_9_out, OP2);
  not not_10 (not_10_out, OP3);
  not not_11 (not_11_out, OP1);
  not not_12 (not_12_out, OP0);
  not not_13 (not_13_out, OP3);
  not not_14 (not_14_out, OP1);
  not not_15 (not_15_out, OP3);
  not not_16 (not_16_out, OP0);
  not not_17 (not_17_out, OP3);
  not not_18 (not_18_out, OP2);
  not not_19 (not_19_out, OP1);
  not not_20 (not_20_out, OP0);
  not not_21 (not_21_out, OP2);
  not not_22 (not_22_out, OP1);
  not not_23 (not_23_out, OP2);
  not not_24 (not_24_out, OP0);
  not not_25 (not_25_out, OP2);
  not not_26 (not_26_out, OP1);
  not not_27 (not_27_out, OP0);
  and _0000 (R_type, not_1_out, not_2_out, not_3_out, not_4_out);
  and _0010 (Imux1, not_5_out, not_6_out, OP1, not_7_out);
  and _0011 (_0011_out, not_8_out, not_9_out, OP1, OP0);
  and _0100 (_0100_out, not_10_out, OP2, not_11_out, not_12_out);
  and _0101 (_0101_out, not_13_out, OP2, not_14_out, OP0);
  and _0110 (ld, not_15_out, OP2, OP1, not_16_out);
  and _0111 (str, not_17_out, OP2, OP1, OP0);
  and _1000 (beq, OP3, not_18_out, not_19_out, not_20_out);
  and _1001 (bne, OP3, not_21_out, not_22_out, OP0);
  and _1010 (bgt, OP3, not_23_out, OP1, not_24_out);
  and _1011 (jump, OP3, not_25_out, OP1, OP0);
  and _1100 (flag, OP3, OP2, not_26_out, not_27_out);
  or or_1 (S1, Imux1, _0011_out, _0100_out);
  or or_2 (S0, _0011_out, beq, bne, bgt);
  or or_3 (Exop, _0101_out, ld, str);
  nor nor_1 (WE, str, beq, bne, bgt, jump, flag);
  or or_4 (PC_1, Imux1, _0011_out, _0100_out, _0101_out, ld, str);
  or or_5 (wpc, beq, bne, bgt, jump);
  or or_6 (muxb, _0011_out, _0100_out, _0101_out, ld, str);

  assign Imux2 = Imux1;
  assign Lmux = ld;
  assign S2 = Imux1;
  assign S3 = 1'b0;
  assign Smux = 1'b0;
endmodule
